# Fritzing sketch Schematic (saved by Fritzing 0.9.3b)
breadboards: 1

parts:
  Segment_Bank_1 = 7 Segment Display
  Segment_Bank_2 = 7 Segment Display
  U1 = 74HC595 [package="DIP16 [THT]"]
  U2 = 74HC595 [package="DIP16 [THT]"]
  U3 = 74HC595 [package="DIP16 [THT]"]
  J1 = female pin header, 2 pins [form="♀ (female)"]
  J2 = female pin header, 2 pins [form="♀ (female)"]
  J3 = female pin header, 2 pins [form="♀ (female)"]
  R1 = Resistor [tolerance=±5% resistance=470 package=THT]
  R2 = Resistor [tolerance=±5% resistance=470 package=THT]

nets:
  N1: Segment_Bank_1.common_anode, R2.Pin_1
  N2: Segment_Bank_2.common_anode, R1.Pin_1
  N3: U1.Q1, R1.Pin_0
  GND: U1.GND, U1.OE, U2.GND, U2.OE, U3.GND, U3.OE, J1.pin2
  N4: U1.Q7', U2.DS
  VCC: U1.MR, U1.VCC, U2.MR, U2.VCC, U3.MR, U3.VCC, J1.pin1
  N5: U1.SH_CP, U2.SH_CP, U3.SH_CP, J3.pin2
  N6: U1.ST_CP, U2.ST_CP, U3.ST_CP, J3.pin1
  N7: U1.DS, J2.pin1
  N8: U1.Q0, R2.Pin_0
  N9: U2.Q7', U3.DS
  N10: U3.Q7', J2.pin2

notes:
  Vcc
  Gnd
  MOSI
  MISO
  SCLK
  CE0
